# Fritzing sketch 32u4_BLE_Switch-v1 (saved by Fritzing 0.9.3b)
circuit board: 8.46667cm x 5.64444cm
breadboards: 1

parts:
  Status_LED = smd LED [color="Red (633nm)" package="0805 [SMD]"]
  S1 = Pushbutton [package="[SMD]"]
  R1 = Resistor [tolerance=±5% resistance=220 package=THT]
  R2 = Resistor [tolerance=±5% resistance=10k package=THT]
  Feather_32u4_BLE = Adafruit Feather 32u4 Bluefruit [part_number="Adafruit #2829"]

nets:
  N1: Status_LED.cathode, R1.Pin_0
  N2: Status_LED.anode, Feather_32u4_BLE.13
  N3: S1.Pin_1, S1.Pin_2, Feather_32u4_BLE.+3V3
  N4: S1.Pin_3, S1.Pin_4, R2.Pin_0, Feather_32u4_BLE.12
  N5: R1.Pin_1, R2.Pin_1, Feather_32u4_BLE.GND

custom parts:
  Adafruit Feather 32u4 Bluefruit: This is the Adafruit Feather 32u4 Bluefruit - our take on an 'all-in-one' Arduino-compatible + Bluetooth Low Energy with built in USB and battery charging. Its an Adafruit Feather 32u4 with a BTLE module, ready to rock! We have other boards in the Feather family, check'em out here. Bluetooth Low Energy is the hottest new low-power, 2.4GHz spectrum wireless protocol. In particular, its the only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

// code stored in the sketch: 32u4_BLE_Switch-TEST.ino
// Pin 13 has an LED connected on most Arduino boards.
// give it a name:
int led = 8;
int btn = 7;

// the setup routine runs once when you press reset:
void setup() {
  // initialize the digital pin as an output.
  pinMode(led, OUTPUT);
  pinMode(btn, INPUT);
  
  Serial.begin(9600);
}

// the loop routine runs over and over again forever:
void loop() {
  
  Serial.println(digitalRead(btn));
  
  if (digitalRead(btn) == HIGH) {
  	digitalWrite(led, HIGH);   // turn the LED on (HIGH is the voltage level)
  } else {
  	digitalWrite(led, LOW);    // turn the LED off by making the voltage LOW
  }
}
